# Fritzing sketch babyduino_no_clock (saved by Fritzing 0.7.11b)
breadboards: 1

parts:
  R2 = Resistor [tolerance=±5% resistance=220 package=THT]
  J1 = male pin header, 2 pins [form="♂ (male)"]
  R1 = Resistor [tolerance=±5% resistance=10k package=THT]
  LED1 = LED - 5mm [color="Red (633nm)" package="5 mm [THT]"]
  IC2 = FTDI [package=SIL]
  IC1 = ATMega8 [package=DIL]

nets:
  N1: R2.Pin_0, IC1.SCK/PB5
  N2: R2.Pin_1, LED1.anode
  GND: J1.pin1, LED1.cathode, IC2.GND/Black, IC1.GND
  N3: J1.pin2, R1.Pin_0, IC1.VCC, IC1.AVCC
  N4: R1.Pin_1, IC1.RESET/PC6
  N5: IC2.TX, IC1.Rx/PD0
  N6: IC2.RX, IC1.Tx/PD1

notes:
  Babyduino, Babyduino (Internal Clock), 1C
