# Fritzing sketch prog_adaptor (saved by Fritzing 0.7.11b)
breadboards: 1

parts:
  IC1 = ATMega8 [package=DIL]
  IC2 = AVRISP [package=SIL]
  R1 = Resistor [tolerance=±5% resistance=10k package=THT]
  C1 = Ceramic Capacitor [capacitance=100nF package="100 mil [THT, multilayer]"]
  Y1 = Resonator [frequency="8 MHz" package=THT]

nets:
  N1: IC1.RESET/PC6, IC2.RST, R1.Pin_0, C1.1
  VCC: IC1.VCC, IC2.VCC, R1.Pin_1
  N2: IC1.GND, C1.0
  N3: IC1.XTAL1/TOSC1/PB6, Y1.0
  N4: IC1.XTAL2/TOSC2/PB7, Y1.pin_1
  N5: IC1.MOSI/OC2/PB3, IC2.MOSI
  N6: IC1.MISO/PB4, IC2.MISO
  N7: IC1.SCK/PB5, IC2.SCK
  GND: IC2.GND#7, Y1.GND

notes:
  AVR ISP Programming Harness, AVR ISP Programming Adaptor, 1D
